// Logisim project alu.circ as structural Verilog: 1 circuit, main circuit alu
module alu (
  input  [31:0] A,
  input  [31:0] B,
  input  [3:0] ALUSel,
  input  [31:0] in_4,
  input  [31:0] in_5,
  input  [31:0] in_6,
  input  [31:0] in_7,
  input  [31:0] in_8,
  input  [31:0] in_9,
  input  [31:0] in_10,
  input  [31:0] in_11,
  input  [31:0] in_12,
  output [31:0] Result,
  output [31:0] out_14,
  output [31:0] out_15,
  output [31:0] out_16,
  output [31:0] out_17,
  output [31:0] out_18,
  output [31:0] out_19,
  output [31:0] out_20,
  output [31:0] out_21,
  output [31:0] out_22,
  output [31:0] out_23,
  output [4:0] out_24,
  output [31:0] out_25
);

  wire comparator_1_lt, comparator_2_gt, comparator_3_lt, comparator_4_gt;
  wire [4:0] bit_extender_1_out, bit_extender_2_out, bit_extender_3_out, bit_extender_6_out;
  wire [31:0] adder_1_out, adder_2_out, adder_3_out, and_1_out, bit_extender_4_out, divider_1_out,
       divider_2_rem, multiplexer_1_out, multiplier_1_cout, multiplier_1_out, multiplier_2_out,
       multiplier_3_cout, not_1_out, not_2_out, or_1_out, shifter_1_out, shifter_2_out, shifter_3_out,
       subtractor_1_out, xor_1_out;

  Bit_Extender #(.in_width(32), .out_width(5)) bit_extender_1 (.in(B), .out(bit_extender_1_out));
  Bit_Extender #(.in_width(32), .out_width(5)) bit_extender_2 (.in(B), .out(bit_extender_2_out));
  Bit_Extender #(.in_width(32), .out_width(5)) bit_extender_3 (.in(B), .out(bit_extender_3_out));
  Multiplier #(.width(32)) multiplier_1 (.a(A), .b(B), .out(multiplier_1_out), .cout(multiplier_1_cout));  // open: cin
  Adder #(.width(32)) adder_1 (.a(A), .b(B), .out(adder_1_out));  // open: cin, cout
  assign and_1_out = A & B;  // AND_Gate and_1, 32 bits wide
  assign or_1_out = A | B;  // OR_Gate or_1, 32 bits wide
  assign xor_1_out = A ^ B;  // XOR_Gate xor_1, 32 bits wide
  Shifter #(.width(32), .shift("lr")) shifter_1 (.in(A), .\dist (bit_extender_1_out), .out(shifter_1_out));
  Shifter #(.width(32), .shift("ar")) shifter_2 (.in(A), .\dist (bit_extender_2_out), .out(shifter_2_out));
  Shifter #(.width(32)) shifter_3 (.in(A), .\dist (bit_extender_3_out), .out(shifter_3_out));
  Comparator #(.width(32)) comparator_1 (.a(A), .b(B), .lt(comparator_1_lt));  // open: gt, eq
  Divider #(.width(32)) divider_1 (.a(A), .b(B), .out(divider_1_out));  // open: upper, rem
  Divider #(.width(32)) divider_2 (.a(A), .b(B), .rem(divider_2_rem));  // open: out, upper
  Multiplier #(.width(32)) multiplier_2 (.a(A), .b(B), .out(multiplier_2_out));  // open: cin, cout
  Multiplier #(.width(32)) multiplier_3 (.a(A), .b(B), .cout(multiplier_3_cout));  // open: out, cin
  Subtractor #(.width(32)) subtractor_1 (.a(A), .b(B), .out(subtractor_1_out));  // open: bin, bout
  assign not_1_out = ~multiplier_1_cout;  // NOT_Gate not_1, 32 bits wide
  Comparator #(.width(32)) comparator_2 (.a({32{1'b0}}), .b(multiplier_1_out), .gt(comparator_2_gt));  // open: eq, lt
  assign bit_extender_4_out = {{31{comparator_1_lt}}, comparator_1_lt};  // Bit_Extender bit_extender_4
  Multiplexer #(.width(32), .enable("false")) multiplexer_1 (
    .in0(multiplier_1_cout), .in1(adder_2_out), .out(multiplexer_1_out), .sel(comparator_2_gt));
  Adder #(.width(32)) adder_2 (.a(not_1_out), .b(32'h1), .out(adder_2_out));  // open: cin, cout
  Multiplexer #(.select(4), .width(32), .enable("false")) multiplexer_2 (
    .in0(adder_1_out), .in1(and_1_out), .in2(or_1_out), .in3(xor_1_out), .in4(shifter_1_out),
    .in5(shifter_2_out), .in6(shifter_3_out), .in7(bit_extender_4_out), .in8(divider_1_out),
    .in9(divider_2_rem), .in10(multiplier_2_out), .in11(multiplier_3_cout), .in12(subtractor_1_out),
    .in13(B), .in14(multiplexer_1_out), .out(Result), .sel(ALUSel));  // open: in15
  Comparator #(.width(32)) comparator_3 (.a(in_5), .b(in_7), .lt(comparator_3_lt));  // open: gt, eq
  assign out_15 = {{31{1'b0}}, comparator_3_lt};  // Bit_Extender bit_extender_5
  Bit_Extender #(.in_width(32), .out_width(5)) bit_extender_6 (.in(in_11), .out(bit_extender_6_out));
  Bit_Extender #(.in_width(32), .out_width(5)) bit_extender_7 (.in(in_12), .out(out_24));
  Shifter #(.width(32), .shift("lr")) shifter_4 (.in(in_8), .\dist (bit_extender_6_out), .out(out_19));
  Multiplier #(.width(32)) multiplier_4 (.a(in_9), .b(in_10), .out(out_16), .cout(out_23));  // open: cin
  assign not_2_out = ~out_23;  // NOT_Gate not_2, 32 bits wide
  Divider #(.width(32)) divider_3 (.a(in_4), .b(in_6), .rem(out_14));  // open: out, upper
  Comparator #(.width(32)) comparator_4 (.a({32{1'b0}}), .b(out_16), .gt(comparator_4_gt));  // open: eq, lt
  Adder #(.width(32)) adder_3 (.a(not_2_out), .b(32'h1), .out(adder_3_out));  // open: cin, cout
  Multiplexer #(.width(32), .enable("false")) multiplexer_3 (
    .in0(out_23), .in1(adder_3_out), .out(out_20), .sel(comparator_4_gt));

  assign out_17 = out_16;
  assign out_18 = in_9;
  assign out_21 = out_20;
  assign out_22 = in_10;
  assign out_25 = out_23;

  // Notes on the sheet:
  //   INPUTS to your circuit
  //   DON'T CHANGE THE LOCATIONS OF THE INPUTS AND OUTPUTS!
  //   OUTPUT from your circuit
endmodule
